// Logisim project 6.1_4.circ as structural Verilog: 1 circuit, main circuit main
module main (
);

  wire controlled_buffer_1_out, undriven, undriven_2;

  assign controlled_buffer_1_out = undriven_2 ? undriven : 1'bz;  // Controlled_Buffer controlled_buffer_1

  // Notes on the sheet:
  //   A
  //   Ena
  //   Tri
endmodule
