// Logisim project experiment_6.1_123.circ as structural Verilog: 1 circuit, main circuit main
module main (
);

  wire and_1_out, not_3_out, or_1_out, undriven, undriven_2;

  // NOT_Gate not_1 is placed but not wired
  // NOT_Gate not_2 is placed but not wired
  or or_1 (or_1_out, undriven, undriven_2);
  and and_1 (and_1_out, undriven, undriven_2);
  not not_3 (not_3_out, undriven);

  // Notes on the sheet:
  //   A
  //   B
endmodule
