// Logisim project 1.circ as structural Verilog: 1 circuit, main circuit main
module main (
  input  in_1,
  output out_2,
  output out_3,
  output out_4,
  output out_5
);

  // OR_Gate _01 is placed but not wired
  // AND_Gate A1 is placed but not wired
  // AND_Gate A2 is placed but not wired
  // AND_Gate A3 is placed but not wired
  // AND_Gate A4 is placed but not wired
endmodule
