// Logisim project selector41.circ as structural Verilog: 1 circuit, main circuit main
module main (
  input  S1,
  input  S2,
  input  [3:0] C0,
  input  [3:0] C1,
  input  [3:0] C2,
  input  [3:0] C3,
  output [3:0] D
);

  wire and_1_out, and_2_out, and_3_out, and_4_out, not_1_out, not_2_out, or_1_out;
  wire [3:0] bit_extender_1_out, bit_extender_2_out;

  assign bit_extender_1_out = {{3{S1}}, S1};  // Bit_Extender bit_extender_1
  assign bit_extender_2_out = {{3{S2}}, S2};  // Bit_Extender bit_extender_2
  not not_1 (not_1_out, bit_extender_1_out[0]);
  not not_2 (not_2_out, bit_extender_2_out[0]);
  and and_1 (and_1_out, not_1_out, not_2_out, C0[0]);
  and and_2 (and_2_out, not_2_out, bit_extender_1_out[0], C1[0]);
  and and_3 (and_3_out, C2[0], not_1_out, bit_extender_2_out[0]);
  and and_4 (and_4_out, bit_extender_1_out[0], bit_extender_2_out[0], C3[0]);
  or or_1 (or_1_out, and_2_out, and_1_out, and_3_out, and_4_out);
  // Pins of 1 and 4 bits meet at C3
  // Pins of 1 and 4 bits meet at C0
  // Pins of 1 and 4 bits meet at C2
  // Pins of 1 and 4 bits meet at bit_extender_2_out
  // Pins of 1 and 4 bits meet at bit_extender_1_out
  // Pins of 1 and 4 bits meet at C1
endmodule
