// Logisim project barrelshifter32.circ as structural Verilog: 2 circuits, main circuit main
module main (
  input  _0,
  input  a0,
  input  a1,
  input  a2,
  input  a3,
  input  a4,
  input  a5,
  input  a6,
  input  a7,
  input  aluc1,
  input  aluc0,
  input  b0,
  input  b1,
  input  b2,
  output c0,
  output c1,
  output c2,
  output c3,
  output c4,
  output c5,
  output c6,
  output c7
);

  wire and_1_out, mux_1_out_4, mux_2_out_4, mux_3_out_4, mux_4_out_4, mux_5_out_4, mux_6_out_4, mux_7_out_4,
       mux_8_out_4, mux_9_out_4, mux_10_out_4, mux_11_out_4, mux_12_out_4, mux_13_out_4, mux_14_out_4,
       mux_15_out_4, mux_16_out_4, mux_17_out_4, mux_18_out_4, mux_19_out_4, mux_20_out_4, mux_21_out_4,
       mux_22_out_4, mux_23_out_4, mux_24_out_4, mux_25_out_4, mux_26_out_4, mux_27_out_4, mux_28_out_4,
       mux_29_out_4, mux_30_out_4, mux_31_out_4, mux_32_out_4, mux_33_out_4, mux_34_out_4, mux_35_out_4,
       mux_36_out_4, mux_37_out_4, mux_38_out_4, mux_39_out_4, mux_40_out_4, not_1_out, not_2_out;

  not not_1 (not_1_out, aluc1);
  MUX mux_1 (.S1(_0), .S2(a1), .in_3(not_2_out), .out_4(mux_1_out_4));
  MUX mux_2 (.S1(a0), .S2(a2), .in_3(not_2_out), .out_4(mux_2_out_4));
  MUX mux_3 (.S1(a1), .S2(a3), .in_3(not_2_out), .out_4(mux_3_out_4));
  MUX mux_4 (.S1(a2), .S2(a4), .in_3(not_2_out), .out_4(mux_4_out_4));
  MUX mux_5 (.S1(a3), .S2(a5), .in_3(not_2_out), .out_4(mux_5_out_4));
  MUX mux_6 (.S1(a4), .S2(a6), .in_3(not_2_out), .out_4(mux_6_out_4));
  MUX mux_7 (.S1(a5), .S2(a7), .in_3(not_2_out), .out_4(mux_7_out_4));
  MUX mux_8 (.S1(a6), .S2(and_1_out), .in_3(not_2_out), .out_4(mux_8_out_4));
  and and_1 (and_1_out, a7, not_1_out);
  not not_2 (not_2_out, aluc0);
  MUX mux_9 (.S1(a0), .S2(mux_1_out_4), .in_3(b0), .out_4(mux_9_out_4));
  MUX mux_10 (.S1(a1), .S2(mux_2_out_4), .in_3(b0), .out_4(mux_10_out_4));
  MUX mux_11 (.S1(a2), .S2(mux_3_out_4), .in_3(b0), .out_4(mux_11_out_4));
  MUX mux_12 (.S1(a3), .S2(mux_4_out_4), .in_3(b0), .out_4(mux_12_out_4));
  MUX mux_13 (.S1(a4), .S2(mux_5_out_4), .in_3(b0), .out_4(mux_13_out_4));
  MUX mux_14 (.S1(a5), .S2(mux_6_out_4), .in_3(b0), .out_4(mux_14_out_4));
  MUX mux_15 (.S1(a6), .S2(mux_7_out_4), .in_3(b0), .out_4(mux_15_out_4));
  MUX mux_16 (.S1(a7), .S2(mux_8_out_4), .in_3(b0), .out_4(mux_16_out_4));
  MUX mux_17 (.S1(_0), .S2(mux_11_out_4), .in_3(not_2_out), .out_4(mux_17_out_4));
  MUX mux_18 (.S1(_0), .S2(mux_12_out_4), .in_3(not_2_out), .out_4(mux_18_out_4));
  MUX mux_19 (.S1(mux_9_out_4), .S2(mux_13_out_4), .in_3(not_2_out), .out_4(mux_19_out_4));
  MUX mux_20 (.S1(mux_10_out_4), .S2(mux_14_out_4), .in_3(not_2_out), .out_4(mux_20_out_4));
  MUX mux_21 (.S1(mux_11_out_4), .S2(mux_15_out_4), .in_3(not_2_out), .out_4(mux_21_out_4));
  MUX mux_22 (.S1(mux_12_out_4), .S2(mux_16_out_4), .in_3(not_2_out), .out_4(mux_22_out_4));
  MUX mux_23 (.S1(mux_9_out_4), .S2(mux_17_out_4), .in_3(b1), .out_4(mux_23_out_4));
  MUX mux_24 (.S1(mux_10_out_4), .S2(mux_18_out_4), .in_3(b1), .out_4(mux_24_out_4));
  MUX mux_25 (.S1(mux_11_out_4), .S2(mux_19_out_4), .in_3(b1), .out_4(mux_25_out_4));
  MUX mux_26 (.S1(mux_12_out_4), .S2(mux_20_out_4), .in_3(b1), .out_4(mux_26_out_4));
  MUX mux_27 (.S1(mux_13_out_4), .S2(mux_21_out_4), .in_3(b1), .out_4(mux_27_out_4));
  MUX mux_28 (.S1(mux_14_out_4), .S2(mux_22_out_4), .in_3(b1), .out_4(mux_28_out_4));
  MUX mux_29 (.S1(mux_15_out_4), .S2(mux_30_out_4), .in_3(b1), .out_4(mux_29_out_4));
  MUX mux_30 (.S1(mux_13_out_4), .S2(and_1_out), .in_3(not_2_out), .out_4(mux_30_out_4));
  MUX mux_31 (.S1(mux_16_out_4), .S2(mux_32_out_4), .in_3(b1), .out_4(mux_31_out_4));
  MUX mux_32 (.S1(mux_14_out_4), .S2(and_1_out), .in_3(not_2_out), .out_4(mux_32_out_4));
  MUX mux_33 (.S1(_0), .S2(mux_27_out_4), .in_3(not_2_out), .out_4(mux_33_out_4));
  MUX mux_34 (.S1(_0), .S2(mux_28_out_4), .in_3(not_2_out), .out_4(mux_34_out_4));
  MUX mux_35 (.S1(_0), .S2(mux_29_out_4), .in_3(not_2_out), .out_4(mux_35_out_4));
  MUX mux_36 (.S1(_0), .S2(mux_31_out_4), .in_3(not_2_out), .out_4(mux_36_out_4));
  MUX mux_37 (.S1(mux_23_out_4), .S2(and_1_out), .in_3(not_2_out), .out_4(mux_37_out_4));
  MUX mux_38 (.S1(mux_24_out_4), .S2(and_1_out), .in_3(not_2_out), .out_4(mux_38_out_4));
  MUX mux_39 (.S1(mux_25_out_4), .S2(and_1_out), .in_3(not_2_out), .out_4(mux_39_out_4));
  MUX mux_40 (.S1(mux_26_out_4), .S2(and_1_out), .in_3(not_2_out), .out_4(mux_40_out_4));
  MUX mux_41 (.S1(mux_23_out_4), .S2(mux_33_out_4), .in_3(b2), .out_4(c0));
  MUX mux_42 (.S1(mux_24_out_4), .S2(mux_34_out_4), .in_3(b2), .out_4(c1));
  MUX mux_43 (.S1(mux_25_out_4), .S2(mux_35_out_4), .in_3(b2), .out_4(c2));
  MUX mux_44 (.S1(mux_26_out_4), .S2(mux_36_out_4), .in_3(b2), .out_4(c3));
  MUX mux_45 (.S1(mux_27_out_4), .S2(mux_37_out_4), .in_3(b2), .out_4(c4));
  MUX mux_46 (.S1(mux_28_out_4), .S2(mux_38_out_4), .in_3(b2), .out_4(c5));
  MUX mux_47 (.S1(mux_29_out_4), .S2(mux_39_out_4), .in_3(b2), .out_4(c6));
  MUX mux_48 (.S1(mux_31_out_4), .S2(mux_40_out_4), .in_3(b2), .out_4(c7));
endmodule

module MUX (
  input  S1,
  input  S2,
  input  in_3,
  output out_4
);

  wire and_1_out, and_2_out, not_1_out;

  and and_1 (and_1_out, S1, not_1_out);
  not not_1 (not_1_out, in_3);
  and and_2 (and_2_out, S2, in_3);
  or or_1 (out_4, and_1_out, and_2_out);
endmodule
