// Logisim project Counter8.circ as structural Verilog: 1 circuit, main circuit main
module main (
  input  rst_n,
  output Q0,
  output Q1,
  output Q2
);

  wire and_1_out, clock_1_out, not_1_out;

  Clock clock_1 (.out(clock_1_out));
  J_K_Flip_Flop j_k_ff_1 (.J(1'b1), .clk(clock_1_out), .K(1'b1), .Q(Q0), .reset(not_1_out));  // open: Qn, preset, en
  not not_1 (not_1_out, rst_n);
  and and_1 (and_1_out, Q0, Q1);
  J_K_Flip_Flop j_k_ff_2 (.J(Q0), .clk(clock_1_out), .K(Q0), .Q(Q1), .reset(not_1_out));  // open: Qn, preset, en
  J_K_Flip_Flop j_k_ff_3 (
    .J(and_1_out), .clk(clock_1_out), .K(and_1_out), .Q(Q2), .reset(not_1_out));  // open: Qn, preset, en

  // Notes on the sheet:
  //   CLK
endmodule
