// Logisim project 6.15_1.circ as structural Verilog: 1 circuit, main circuit main
module main (
  input  CLK1,
  input  [7:0] in_2,
  output out_3
);

  wire A_q, A_qn, ADD, adder_1_cout, and_1_out, and_2_out, and_3_out, and_4_out, and_6_out, B_q, B_qn, CLK2,
       LDA, LDB, minus_CLR, nor_1_out, or_1_out, or_2_out;
  wire [7:0] adder_1_out, controlled_buffer_1_out, register_1_q, register_2_q;

  and and_1 (and_1_out, CLK2, LDA);
  and and_2 (and_2_out, CLK2, LDB);
  or or_1 (or_1_out, A_qn, B_qn);
  or or_2 (or_2_out, A_q, B_q);
  Register register_1 (.D(in_2), .Q(register_1_q), .clk(and_1_out));  // open: en, clr
  D_Flip_Flop A (.clk(CLK1), .D(or_1_out), .Q(A_q), .Qn(A_qn));  // open: preset, en, reset
  D_Flip_Flop B (.clk(CLK1), .D(or_2_out), .Q(B_q), .Qn(B_qn));  // open: preset, en, reset
  Register register_2 (.D(adder_1_out), .Q(register_2_q), .clk(and_2_out));  // open: en, clr
  and and_3 (and_3_out, A_qn, B_qn);
  and and_4 (and_4_out, A_q, B_q);
  assign controlled_buffer_1_out = ADD ? register_2_q : 8'bz;  // Controlled_Buffer controlled_buffer_1
  or or_3 (LDA, and_3_out, and_4_out);
  xor xor_1 (LDB, A_q, B_q);
  and and_5 (ADD, B_q, A_qn);
  Adder adder_1 (.a(register_1_q), .b(controlled_buffer_1_out), .out(adder_1_out), .cout(adder_1_cout));  // open: cin
  not not_1 (CLK2, CLK1);
  nor nor_1 (nor_1_out, B_q, A_q);
  not not_2 (minus_CLR, nor_1_out);
  Register #(.width(1)) register_3 (.D(adder_1_cout), .en(minus_CLR), .Q(out_3), .clk(and_6_out));  // open: clr
  and and_6 (and_6_out, ADD, CLK2);
endmodule
