// Logisim project 6.15_2.circ as structural Verilog: 1 circuit, main circuit main
module main (
  input  CLK1,
  input  in_2,
  input  in_3,
  input  in_4,
  input  in_5,
  input  in_6,
  input  in_7,
  input  in_8,
  input  in_9,
  input  [7:0] in_10,
  output out_11
);

  wire A, ADD, adder_1_cout, and_1_out, and_2_out, and_3_out, and_4_out, and_6_out, \A反 , B, \B反 , CLK2, LDA,
       LDB, minus_CLR, multiplexer_1_out, multiplexer_2_out, nor_1_out;
  wire [7:0] adder_1_out, controlled_buffer_1_out, register_1_q, register_2_q;

  and and_1 (and_1_out, CLK2, LDA);
  and and_2 (and_2_out, CLK2, LDB);
  Multiplexer #(.select(2), .enable("false")) multiplexer_1 (
    .in0(in_2), .in1(in_3), .in2(in_4), .in3(in_5), .out(multiplexer_1_out), .sel({B, A}));
  Multiplexer #(.select(2), .enable("false")) multiplexer_2 (
    .in0(in_6), .in1(in_7), .in2(in_8), .in3(in_9), .out(multiplexer_2_out), .sel({B, A}));
  Register register_1 (.D(in_10), .Q(register_1_q), .clk(and_1_out));  // open: en, clr
  D_Flip_Flop u_A (.clk(CLK1), .D(multiplexer_1_out), .Q(A), .Qn(\A反 ));  // open: preset, en, reset
  D_Flip_Flop u_B (.clk(CLK1), .D(multiplexer_2_out), .Q(B), .Qn(\B反 ));  // open: preset, en, reset
  Register register_2 (.D(adder_1_out), .Q(register_2_q), .clk(and_2_out));  // open: en, clr
  assign controlled_buffer_1_out = ADD ? register_2_q : 8'bz;  // Controlled_Buffer controlled_buffer_1
  Adder adder_1 (.a(register_1_q), .b(controlled_buffer_1_out), .out(adder_1_out), .cout(adder_1_cout));  // open: cin
  and and_3 (and_3_out, A, B);
  and and_4 (and_4_out, \A反 , \B反 );
  or or_1 (LDA, and_3_out, and_4_out);
  xor xor_1 (LDB, A, B);
  and and_5 (ADD, \A反 , B);
  Register #(.width(1)) register_3 (.D(adder_1_cout), .en(minus_CLR), .Q(out_11), .clk(and_6_out));  // open: clr
  nor nor_1 (nor_1_out, A, B);
  and and_6 (and_6_out, ADD, CLK2);
  not not_1 (CLK2, CLK1);
  not not_2 (minus_CLR, nor_1_out);
endmodule
