// Logisim project 6.15_3.circ as structural Verilog: 1 circuit, main circuit main
module main (
  input  CLK1,
  input  [7:0] in_2,
  output out_3
);

  wire A, ADD, adder_1_cout, and_1_out, and_2_out, and_3_out, and_4_out, and_6_out, \A反 , B, \B反 , CLK2, LDA,
       LDB, minus_CLR, nor_1_out, not_1_out, or_1_out, or_2_out, Qa_q, Qb_q, Qc_q, Qd_q;
  wire [7:0] adder_1_out, controlled_buffer_1_out, register_1_q, register_2_q;

  and and_1 (and_1_out, CLK2, LDA);
  and and_2 (and_2_out, CLK2, LDB);
  not not_1 (not_1_out, or_1_out);
  or or_1 (or_1_out, Qa_q, Qb_q, Qc_q, Qd_q);
  or or_2 (or_2_out, Qb_q, Qd_q);
  D_Flip_Flop Qa (.clk(CLK1), .D(not_1_out), .Q(Qa_q));  // open: Qn, preset, en, reset
  D_Flip_Flop Qb (.clk(CLK1), .D(Qa_q), .Q(Qb_q));  // open: Qn, preset, en, reset
  D_Flip_Flop Qc (.clk(CLK1), .D(or_2_out), .Q(Qc_q));  // open: Qn, preset, en, reset
  D_Flip_Flop Qd (.clk(CLK1), .D(Qc_q), .Q(Qd_q));  // open: Qn, preset, en, reset
  Register register_1 (.D(in_2), .Q(register_1_q), .clk(and_1_out));  // open: en, clr
  or or_3 (A, Qb_q, Qc_q);
  or or_4 (B, Qc_q, Qd_q);
  Register register_2 (.D(adder_1_out), .Q(register_2_q), .clk(and_2_out));  // open: en, clr
  not not_2 (\A反 , A);
  not not_3 (\B反 , B);
  assign controlled_buffer_1_out = ADD ? register_2_q : 8'bz;  // Controlled_Buffer controlled_buffer_1
  Adder adder_1 (.a(register_1_q), .b(controlled_buffer_1_out), .out(adder_1_out), .cout(adder_1_cout));  // open: cin
  and and_3 (and_3_out, A, B);
  and and_4 (and_4_out, \A反 , \B反 );
  or or_5 (LDA, and_3_out, and_4_out);
  xor xor_1 (LDB, A, B);
  and and_5 (ADD, \A反 , B);
  Register #(.width(1)) register_3 (.D(adder_1_cout), .en(minus_CLR), .Q(out_3), .clk(and_6_out));  // open: clr
  nor nor_1 (nor_1_out, A, B);
  and and_6 (and_6_out, ADD, CLK2);
  not not_4 (CLK2, CLK1);
  not not_5 (minus_CLR, nor_1_out);
endmodule
