// Logisim project 6.18_1（2）.circ as structural Verilog: 1 circuit, main circuit main
module main (
  input  \初始清零 ,
  input  clk1,
  input  [7:0] in_3,
  input  in_4
);

  wire A_B, \A_B反 , and_1_out, and_2_out, CAP, clk2, LDRA, LDRB, nand_1_out, nor_1_out, or_1_out, or_2_out,
       Qa, \Qa反 , Qb, \Qb反 , Qc, \Qc反 , \Qd反 ;
  wire [7:0] controlled_buffer_1_out, controlled_buffer_2_out, RA_q, RB_q;

  and and_1 (and_1_out, CAP, \A_B反 );
  and and_2 (and_2_out, CAP, A_B);
  nor nor_1 (nor_1_out, Qb, Qa, CAP, Qc);
  or or_1 (or_1_out, and_1_out, Qa);
  or or_2 (or_2_out, and_2_out, Qb);
  D_Flip_Flop a (.clk(clk1), .D(nor_1_out), .Q(Qa), .Qn(\Qa反 ), .en(\初始清零 ), .reset(\初始清零 ));  // open: preset
  D_Flip_Flop b (.clk(clk1), .D(or_1_out), .Q(Qb), .Qn(\Qb反 ), .reset(\初始清零 ));  // open: preset, en
  D_Flip_Flop c (.clk(clk1), .D(or_2_out), .Q(Qc), .Qn(\Qc反 ), .reset(\初始清零 ));  // open: preset, en
  D_Flip_Flop d (.clk(clk1), .D(Qc), .Q(CAP), .Qn(\Qd反 ), .reset(\初始清零 ));  // open: preset, en
  not not_1 (clk2, clk1);
  nand nand_1 (nand_1_out, \Qa反 , \Qc反 );
  and and_3 (LDRA, clk2, Qb);
  Counter RA (.D(RB_q), .Q(RA_q), .clk(LDRA), .clr(in_4));  // open: load, count, carry
  Register RB (.D(in_3), .Q(RB_q), .clk(LDRB), .clr(in_4));  // open: en
  and and_4 (LDRB, nand_1_out, clk2);
  assign controlled_buffer_1_out = CAP ? RA_q : 8'bz;  // Controlled_Buffer controlled_buffer_1
  assign controlled_buffer_2_out = CAP ? RB_q : 8'bz;  // Controlled_Buffer controlled_buffer_2
  Comparator comparator_1 (
    .a(controlled_buffer_1_out), .b(controlled_buffer_2_out), .gt(A_B), .eq(\A_B反 ), .lt(\A_B反 ));

  // Other names for the same wires on the sheet: Qd = CAP
endmodule
