// Logisim project 6.15多路选择器型.circ as structural Verilog: 1 circuit, main circuit main
module main (
  input  [7:0] in_1,
  input  in_2,
  input  in_3,
  output out_4,
  output [7:0] out_5
);

  wire A, ADD, and_1_out, and_2_out, and_3_out, B, clock_1_out, CLR, LDA, LDB, multiplexer_1_out,
       multiplexer_2_out, not_2_out, not_3_out, not_4_out, OverFlow, T2;
  wire [7:0] controlled_buffer_1_out, register_2_q, register_3_q;

  not not_1 (T2, clock_1_out);
  Clock clock_1 (.out(clock_1_out));
  Register #(.width(1)) register_1 (.D(OverFlow), .Q(out_4), .clk(and_1_out), .clr(CLR));  // open: en
  and and_1 (and_1_out, ADD, T2);
  Register register_2 (.D(in_1), .Q(register_2_q), .clk(and_2_out), .clr(CLR));  // open: en
  and and_2 (and_2_out, LDA, T2);
  not not_2 (not_2_out, in_2);
  Adder adder_1 (.a(register_2_q), .b(controlled_buffer_1_out), .out(out_5), .cout(OverFlow));  // open: cin
  assign controlled_buffer_1_out = ADD ? register_3_q : 8'bz;  // Controlled_Buffer controlled_buffer_1
  Multiplexer #(.select(2)) multiplexer_1 (
    .in0(not_2_out), .in1(in_2), .in2(in_2), .in3(in_2), .out(multiplexer_1_out), .sel({A, B}));  // open: en
  Register register_3 (.D(out_5), .Q(register_3_q), .clk(and_3_out), .clr(CLR));  // open: en
  and and_3 (and_3_out, T2, LDB);
  D_Flip_Flop d_ff_1 (.clk(clock_1_out), .D(multiplexer_1_out), .Q(A));  // open: Qn, preset, en, reset
  not not_3 (not_3_out, B);
  Multiplexer #(.select(2)) multiplexer_2 (
    .in0(in_3), .in1(in_3), .in2(in_3), .in3(not_4_out), .out(multiplexer_2_out), .sel({A, B}));  // open: en
  not not_4 (not_4_out, in_3);
  xnor xnor_1 (LDA, A, B);
  nor nor_1 (CLR, A, B);
  xor xor_1 (LDB, A, B);
  and and_4 (ADD, A, not_3_out);
  D_Flip_Flop d_ff_2 (.clk(clock_1_out), .D(multiplexer_2_out), .Q(B));  // open: Qn, preset, en, reset
endmodule
