// Logisim project 6.15定序型.circ as structural Verilog: 1 circuit, main circuit main
module main (
  input  [7:0] in_1,
  output out_2,
  output [7:0] out_3
);

  wire ADD, and_1_out, and_2_out, and_3_out, CLR, LDA, LDB, not_1_out, or_1_out, or_2_out, OverFlow, QB, QC,
       T2;
  wire [7:0] controlled_buffer_1_out, register_2_q, register_3_q;

  Register #(.width(1)) register_1 (.D(OverFlow), .Q(out_2), .clk(and_1_out), .clr(CLR));  // open: en
  and and_1 (and_1_out, ADD, T2);
  or or_1 (or_1_out, CLR, QB, QC, ADD);
  Register register_2 (.D(in_1), .Q(register_2_q), .clk(and_2_out), .clr(CLR));  // open: en
  and and_2 (and_2_out, T2, LDA);
  not not_1 (not_1_out, or_1_out);
  Clock clock_1 (.out(T2));
  assign controlled_buffer_1_out = ADD ? register_3_q : 8'bz;  // Controlled_Buffer controlled_buffer_1
  D_Flip_Flop d_ff_1 (.clk(T2), .D(not_1_out), .Q(CLR));  // open: Qn, preset, en, reset
  Adder adder_1 (.a(register_2_q), .b(controlled_buffer_1_out), .out(out_3), .cout(OverFlow));  // open: cin
  Register register_3 (.D(out_3), .Q(register_3_q), .clk(and_3_out), .clr(CLR));  // open: en
  and and_3 (and_3_out, T2, LDB);
  D_Flip_Flop d_ff_2 (.clk(T2), .D(CLR), .Q(QB));  // open: Qn, preset, en, reset
  or or_2 (or_2_out, QB, ADD);
  D_Flip_Flop d_ff_3 (.clk(T2), .D(or_2_out), .Q(QC));  // open: Qn, preset, en, reset
  or or_3 (LDA, CLR, QC);
  or or_4 (LDB, QB, ADD);
  D_Flip_Flop d_ff_4 (.clk(T2), .D(QC), .Q(ADD));  // open: Qn, preset, en, reset

  // Other names for the same wires on the sheet: QA = CLR; QD = ADD
endmodule
